# Fritzing sketch Circuit (saved by Fritzing 0.9.3b)

parts:
  Part1 = Arduino Uno (Rev3)
  Candidate_7 = Round Pushbutton
  Candidate_10 = Round Pushbutton
  Candidate_4 = Round Pushbutton
  Candidate_9 = Round Pushbutton
  Candidate_8 = Round Pushbutton
  Candidate_6 = Round Pushbutton
  Candidate_5 = Round Pushbutton
  Candidate_3 = Round Pushbutton
  Candidate_2 = Round Pushbutton
  Candidate_1 = Round Pushbutton
  CLEAR = Round Pushbutton
  RESULT = Round Pushbutton
  R1 = Resistor [tolerance=±5% resistance=10k package=THT]
  R2 = Resistor [tolerance=±5% resistance=10k package=THT]
  Part2 = LCD1602-I2C
  Buzzer = Piezo Speaker
  READY_TO_VOTE = smd LED [color="Green (565nm)" package="1206 [SMD]"]
  R3 = Resistor [tolerance=±5% resistance=330 package=THT]

nets:
  N1: Part1.A0, Buzzer.pin2
  N2: Part1.A1, R3.Pin_0
  N3: Part1.A2, RESULT.leg1, R1.Pin_1
  N4: Part1.A4/SDA, Part2.SDA
  N5: Part1.A5/SCL, Part2.SCL
  N6: Part1.D8, Candidate_9.leg0
  N7: Part1.D9_PWM, Candidate_10.leg0
  N8: Part1.D0/RX, Candidate_1.leg0
  N9: Part1.D1/TX, Candidate_2.leg0
  N10: Part1.D2, Candidate_3.leg0
  N11: Part1.D3_PWM, Candidate_4.leg0
  N12: Part1.D4, Candidate_5.leg0
  N13: Part1.D5_PWM, Candidate_6.leg0
  N14: Part1.D6_PWM, Candidate_7.leg0
  N15: Part1.D7, Candidate_8.leg0
  5V: Part1.5V, CLEAR.leg0, RESULT.leg0, Part2.VCC
  N16: Part1.GND, Candidate_7.leg1, Candidate_10.leg1, Candidate_4.leg1, Candidate_9.leg1, Candidate_8.leg1, Candidate_6.leg1, Candidate_5.leg1, Candidate_3.leg1, Candidate_2.leg1, Candidate_1.leg1, R1.Pin_0, R2.Pin_0, Buzzer.pin1, READY_TO_VOTE.cathode
  N17: CLEAR.leg1, R2.Pin_1

custom parts:
  LCD1602-I2C: A standard character display, usually with 2x16 characters. Comes in many colors with LCM1602 IIC attached.
